# Fritzing sketch wiring (saved by Fritzing 0.9.0b)

parts:
  LCD1 = LCD screen
  Part1 = Arduino Yun
  KEYPAD1 = Membrane Matrix Keypad
  POT1 = Breadboard Trimpot

nets:
  VSS: LCD1.VSS, LCD1.R/W, LCD1.LED-, Part1.GND, POT1.PIN3
  VDD: LCD1.VDD, Part1.5V, POT1.PIN1
  N1: LCD1.V0, POT1.PIN2
  N2: LCD1.RS, Part1.A5/SCL
  N3: LCD1.E, Part1.A4/SDA
  N4: LCD1.DB4, Part1.A3
  N5: LCD1.DB5, Part1.A2
  N6: LCD1.DB6, Part1.A1
  N7: LCD1.DB7, Part1.A0
  N8: LCD1.LED+, Part1.D13/SCK
  N9: Part1.D8, KEYPAD1.1
  N10: Part1.D2, KEYPAD1.7
  N11: Part1.D3_PWM, KEYPAD1.6
  N12: Part1.D4, KEYPAD1.5
  N13: Part1.D5_PWM, KEYPAD1.4
  N14: Part1.D6_PWM, KEYPAD1.3
  N15: Part1.D7, KEYPAD1.2

custom parts:
  Membrane Matrix Keypad: Membrane Matrix 3x4 Keypad
